# Fritzing sketch Marimba16Tablas_protoboard (saved by Fritzing 0.9.3b)
breadboards: 1

parts:
  Parte1 = Arduino Mega 2560 (Rev3)
  R1 = Resistor [tolerance=±5% resistance=560k package=THT]
  R2 = Resistor [tolerance=±5% resistance=560k package=THT]
  R3 = Resistor [tolerance=±5% resistance=560k package=THT]
  R4 = Resistor [tolerance=±5% resistance=560k package=THT]
  R5 = Resistor [tolerance=±5% resistance=560k package=THT]
  R6 = Resistor [tolerance=±5% resistance=560k package=THT]
  R7 = Resistor [tolerance=±5% resistance=560k package=THT]
  R8 = Resistor [tolerance=±5% resistance=560k package=THT]
  R9 = Resistor [tolerance=±5% resistance=560k package=THT]
  R10 = Resistor [tolerance=±5% resistance=560k package=THT]
  R11 = Resistor [tolerance=±5% resistance=560k package=THT]
  R12 = Resistor [tolerance=±5% resistance=560k package=THT]
  R13 = Resistor [tolerance=±5% resistance=560k package=THT]
  R14 = Resistor [tolerance=±5% resistance=560k package=THT]
  R15 = Resistor [tolerance=±5% resistance=560k package=THT]
  R16 = Resistor [tolerance=±5% resistance=560k package=THT]
  J2 = shrouded pin header, 40 pins [form="♂ (shrouded male)"]
  Raspberry_Pi1 = Raspberry Pi 2  # not connected
  J3 = Piezo Speaker  # not connected

nets:
  N1: Parte1.A8, R9.Pin_1, J2.pin32
  N2: Parte1.A9, R10.Pin_1, J2.pin31
  N3: Parte1.A10, R11.Pin_1, J2.pin30
  N4: Parte1.A11, R12.Pin_1, J2.pin29
  N5: Parte1.A12, R13.Pin_1, J2.pin28
  N6: Parte1.A13, R14.Pin_1, J2.pin27
  N7: Parte1.A14, R15.Pin_1, J2.pin26
  N8: Parte1.A15, R16.Pin_1, J2.pin25
  N9: Parte1.A0, R1.Pin_1, J2.pin40
  N10: Parte1.A1, R2.Pin_1, J2.pin39
  N11: Parte1.A2, R3.Pin_1, J2.pin38
  N12: Parte1.A3, R4.Pin_1, J2.pin37
  N13: Parte1.A4, R5.Pin_1, J2.pin36
  N14: Parte1.A5, R6.Pin_1, J2.pin35
  N15: Parte1.A6, R7.Pin_1, J2.pin34
  N16: Parte1.A7, R8.Pin_1, J2.pin33
  N17: Parte1.GND, R1.Pin_0, R2.Pin_0, R3.Pin_0, R4.Pin_0, R5.Pin_0, R6.Pin_0, R7.Pin_0, R8.Pin_0, R9.Pin_0, R10.Pin_0, R11.Pin_0, R12.Pin_0, R13.Pin_0, R14.Pin_0, R15.Pin_0, R16.Pin_0, J2.pin1, J2.pin2, J2.pin3, J2.pin4, J2.pin5, J2.pin6, J2.pin7, J2.pin8, J2.pin9, J2.pin10, J2.pin11, J2.pin12, J2.pin13, J2.pin14, J2.pin15, J2.pin16

notes:
  Piezoeléctrico
  sensor de
  vibración
  Cable ribbon hacia los
  16 piezoelectricos
  Cable USB entre
  Arduino y Raspberry
  MARIMBA INCLUSIVA - 16 TABLAS
